# Fritzing sketch ektp RFID (saved by Fritzing 0.9.2b)
breadboards: 1

parts:
  Part1 = Arduino Uno (Rev3)
  Part2 = RFID-RC522-v2
  LED1 = smd LED [color="Yellow (595nm)" package="0805 [SMD]"]
  LED5 = smd LED [color="Red (633nm)" package="0603 [SMD]"]
  R1 = Resistor [tolerance=±5% resistance=220 package="0402 [SMD]"]
  R2 = Resistor [tolerance=±5% resistance=220 package="0402 [SMD]"]
  R3 = Resistor [tolerance=±5% resistance=220 package="0402 [SMD]"]
  LED6 = smd LED [color="Green (570nm)" package="0805 [SMD]"]
  U1 = LCD-16X2 [package=lcd-16x2_nosilk]
  U2 = POT [package=pot_alpha_rv16af-20]
  R5 = Resistor [tolerance=±5% resistance=220 package="0402 [SMD]"]

nets:
  N1: Part1.A0, R1.Pin_0
  N2: Part1.A1, R2.Pin_0
  N3: Part1.A2, R3.Pin_0
  N4: Part1.D9_PWM, Part2.RST
  N5: Part1.D10_PWM/SS, Part2.SDA
  N6: Part1.D11_PWM/MOSI, Part2.MOSI
  N7: Part1.D12/MISO, Part2.MISO
  N8: Part1.D13/SCK, Part2.SCK
  GND: Part1.GND, Part2.GND, LED1.cathode, LED5.cathode, LED6.cathode, U1.VSS, U1.R_W, U1.K, U2.A
  N9: Part1.D2, U1.RS
  N10: Part1.D3_PWM, U1.E
  N11: Part1.D4, U1.DB4
  N12: Part1.D5_PWM, U1.DB5
  N13: Part1.D6_PWM, U1.DB6
  N14: Part1.D7, U1.DB7
  3V3: Part1.3V3, Part2.3.3V
  5V: Part1.5V, U1.VDD, U2.E, R5.Pin_0
  N15: LED1.anode, R2.Pin_1
  N16: LED5.anode, R1.Pin_1
  N17: R3.Pin_1, LED6.anode
  N18: U1.VO, U2.S
  N19: U1.A, R5.Pin_1

custom parts:
  RFID-RC522-v2: A simple China made RFID-RC522 Reader; do check the pin labels, as this is a MFRC522 based clone.
